// Logisim project Basic_Circuits (XOR,Adders).circ as structural Verilog: 10 circuits, main circuit main
module main (
  input  in_1,
  input  in_2,
  input  in_3,
  input  in_4,
  input  in_5,
  input  in_6
);

  Three_bit_adder three_bit_adder_1 ();  // open: A, B, S1, S2, S4, S8
  Two_Bit_Adder two_bit_adder_1 ();  // open: A, B, S4, S1, S2
endmodule

module Four_Bit_Adder (
  input  [3:0] A,
  input  [3:0] B,
  output S1,
  output S2,
  output S4,
  output S8,
  output S16
);

  wire half_adder_1_carry, half_adder_2_carry, half_adder_3_carry, two_bit_adder_variation_1_s4,
       two_bit_adder_variation_2_s1, two_bit_adder_variation_2_s2, two_bit_adder_variation_2_s4;

  Two_Bit_Adder_Variation two_bit_adder_variation_1 (
    .A(A[1:0]), .B(B[1:0]), .S1(S1), .S2(S2), .S4(two_bit_adder_variation_1_s4));
  Two_Bit_Adder_Variation two_bit_adder_variation_2 (
    .A(B[3:2]), .B(A[3:2]), .S1(two_bit_adder_variation_2_s1), .S2(two_bit_adder_variation_2_s2),
    .S4(two_bit_adder_variation_2_s4));
  Half_Adder half_adder_1 (
    .A(two_bit_adder_variation_1_s4), .B(two_bit_adder_variation_2_s1), .Sum(S4), .Carry(half_adder_1_carry));
  Half_Adder half_adder_2 (
    .A(half_adder_1_carry), .B(two_bit_adder_variation_2_s2), .Sum(S8), .Carry(half_adder_2_carry));
  Half_Adder half_adder_3 (
    .A(half_adder_2_carry), .B(two_bit_adder_variation_2_s4), .Sum(S16), .Carry(half_adder_3_carry));

  // Notes on the sheet:
  //   Adding bit 2 and bit 3, by first splitting the 4 bit input into two 2 bit sets
  //   Adding bit 0 and 1 , by first splitting the 4 bit input into two 2 bits sets.
  //   S1 and S2 produced by adding the bit 0 and bit 1 from A and B
  //   S16 produced by summing the carry produced by sumuation of Bit 2 and Bit 3 of A and B, and the carry produced during the S8 production
  //   S4 produced by adding the carry ,produced by S1 and S2 sum, with the Sum bit 1 produced by summing the bit 2 from A and B
  //   S8 produced in a similar fashion as S4, just the carry used is of S4 sum, and the other bit is the result of adding bit 3 of A and B.
endmodule

module Half_Adder (
  input  A,
  input  B,
  output Sum,
  output Carry
);

  xor xor_1 (Sum, A, B);
  and and_1 (Carry, A, B);
endmodule

module Full_adder (
  input  in_1,
  input  in_2,
  input  in_3,
  input  A,
  input  B,
  input  C_in,
  output out_7,
  output Interim_sum,
  output C_out,
  output Final_Sum
);

  wire and_1_out, and_2_out, half_adder_1_carry, half_adder_2_carry, xor_1_out, xor_2_out;

  xor xor_1 (xor_1_out, in_1, in_2);
  and and_1 (and_1_out, in_1, in_2);
  xor xor_2 (xor_2_out, in_3, xor_1_out);
  and and_2 (and_2_out, in_3, xor_1_out);
  Half_Adder half_adder_1 (.A(A), .B(B), .Sum(Interim_sum), .Carry(half_adder_1_carry));
  Half_Adder half_adder_2 (.A(Interim_sum), .B(C_in), .Sum(Final_Sum), .Carry(half_adder_2_carry));
  LED led_1 (.in(Final_Sum));
  or or_1 (out_7, and_1_out, and_2_out);
  or or_2 (C_out, half_adder_1_carry, half_adder_2_carry);
  LED led_2 (.in(C_out));
endmodule

module XOR_Gate (
  input  A,
  input  B,
  output Ans
);

  wire and_1_out, not_1_out, not_2_out, or_1_out, or_2_out, or_3_out;

  or or_1 (or_1_out, A, B);
  not not_1 (not_1_out, A);
  not not_2 (not_2_out, B);
  and and_1 (and_1_out, A, B);
  or or_2 (or_2_out, not_1_out, not_2_out);
  or or_3 (or_3_out, and_1_out, or_1_out);
  and and_2 (Ans, or_3_out, or_2_out);

  // Notes on the sheet:
  //   XOR gate = [ (A AND B) OR (A OR B) ] AND (NOT A OR NOT B)
endmodule

module Full_adder_simple (
  input  in_1,
  input  in_2,
  input  in_3,
  output out_4,
  output out_5
);

  wire and_1_out, and_2_out, xor_1_out;

  xor xor_1 (xor_1_out, in_1, in_2);
  and and_1 (and_1_out, in_1, in_2);
  xor xor_2 (out_5, in_3, xor_1_out);
  and and_2 (and_2_out, in_3, xor_1_out);
  or or_1 (out_4, and_1_out, and_2_out);
endmodule

module Xor_Gate_For_Three (
  input  A,
  input  B,
  input  C,
  output Interim_Ans,
  output Ans
);

  XOR_Gate xor_gate_1 (.A(A), .B(B), .Ans(Interim_Ans));
  XOR_Gate xor_gate_2 (.A(Interim_Ans), .B(C), .Ans(Ans));
endmodule

module Two_Bit_Adder (
  input  [1:0] A,
  input  [1:0] B,
  output S4,
  output S1,
  output S2
);

  wire half_adder_1_carry, half_adder_2_carry, half_adder_2_sum, half_adder_3_carry;

  Half_Adder half_adder_1 (.A(A[0]), .B(B[0]), .Sum(S1), .Carry(half_adder_1_carry));
  Half_Adder half_adder_2 (.A(A[1]), .B(B[1]), .Sum(half_adder_2_sum), .Carry(half_adder_2_carry));
  xor xor_1 (S4, half_adder_2_carry, half_adder_3_carry);
  Half_Adder half_adder_3 (.A(half_adder_2_sum), .B(half_adder_1_carry), .Sum(S2), .Carry(half_adder_3_carry));

  // Notes on the sheet:
  //   Inputting the first bits of both the numbers
  //   Inputting the second bits of all the numbers
  //   Bit 1
  //   Summed the carries produced by the: sumation of first and second bits, and the sumation of second bits .
  //   The carry of the first bits , summed with the sum of the second bits
  //   Bit 3
  //   Bit 2
endmodule

module Two_Bit_Adder_Variation (
  input  [1:0] A,
  input  [1:0] B,
  output S1,
  output S2,
  output S4
);

  wire half_adder_1_carry;

  Half_Adder half_adder_1 (.A(A[0]), .B(B[0]), .Sum(S1), .Carry(half_adder_1_carry));
  Full_adder full_adder_1 (
    .A(A[1]), .B(B[1]), .C_in(half_adder_1_carry), .C_out(S4), .Final_Sum(S2));  // open: in_1, in_2, in_3, out_7, Interim_sum
endmodule

module Three_bit_adder (
  input  [2:0] A,
  input  [2:0] B,
  output S1,
  output S2,
  output S4,
  output S8
);

  wire two_bit_adder_variation_1_s2;

  Two_Bit_Adder_Variation two_bit_adder_variation_1 (
    .A(A[1:0]), .B(B[1:0]), .S1(S1), .S2(two_bit_adder_variation_1_s2), .S4(S2));
  Full_adder full_adder_1 (
    .A(B[2]), .B(A[2]), .C_in(two_bit_adder_variation_1_s2), .C_out(S8), .Final_Sum(S4));  // open: in_1, in_2, in_3, out_7, Interim_sum
endmodule
